# Fritzing sketch Innlevering1 (saved by Fritzing 0.9.2b)
breadboards: 2

parts:
  U1 = MAX7219 [package=dil24]
  Part1 = Arduino Uno (Rev3) - ICSP
  R2 = Resistor [tolerance=±5% resistance=10k package=THT]
  R3 = Resistor [tolerance=±5% resistance=10k package=THT]
  R4 = Resistor [tolerance=±5% resistance=10k package=THT]
  R5 = Resistor [tolerance=±5% resistance=10k package=THT]
  T1 = LM35 Temperature Sensor [package="TO92 [THT]"]
  S1 = Pushbutton [package="[THT]"]
  R6 = Resistor [tolerance=±5% resistance=220 package=THT]
  J1 = Piezo Speaker  # not connected
  R7 = Resistor [tolerance=±5% resistance=220 package=THT]
  LED1 = LED - 5mm [color="Blue (525nm)" package="5 mm [THT]"]
  R8 = Resistor [tolerance=±5% resistance=220 package=THT]

nets:
  N1: U1.DIN, Part1.D8
  GND: U1.GND, U1.GND2, Part1.GND, T1.GND, R6.Pin_0, R7.Pin_0, R8.Pin_0
  N2: U1.LOAD, Part1.D9_PWM
  N3: U1.CLK, Part1.D10_PWM/SS
  N4: U1.ISET, R5.Pin_0
  VCC: U1.VCC, Part1.5V, R2.Pin_0, T1.+Vs
  N5: Part1.A0, T1.Vout
  N6: Part1.D13/SCK, LED1.anode
  N7: Part1.D2, S1.Pin_1, S1.Pin_2, R6.Pin_1
  N8: R2.Pin_1, R3.Pin_1
  N9: R3.Pin_0, R4.Pin_1
  N10: R4.Pin_0, R5.Pin_1
  N11: S1.Pin_3, S1.Pin_4
  N12: LED1.cathode, R8.Pin_1

notes:
  Her står SMM-1588 matrise med 12 pinner på hver side, jeg fant ikke passende detalj i Fritzing, som ikke dekket halvparten av breadboard og ikke gjemte alt annet.
  Piezo buzzer er ikke akkurat den samme nok
  Skulle helst bruke 1 * 40K motstand, om jeg hadde den, så måtte seriekoble 4 * 10K Ohm.
